// Logisim project 32x32-bit-register-file.circ as structural Verilog: 2 circuits, main circuit main
module main (
  input  [31:0] BusW,
  input  [4:0] RW,
  input  RegWrite,
  output [31:0] out_4,
  output [31:0] out_5,
  output [31:0] out_6,
  output [31:0] out_7,
  output [31:0] out_8,
  output [31:0] out_9,
  output [31:0] out_10,
  output [31:0] out_11,
  output [31:0] out_12,
  output [31:0] out_13,
  output [31:0] out_14,
  output [31:0] out_15,
  output [31:0] out_16,
  output [31:0] out_17,
  output [31:0] out_18,
  output [31:0] out_19,
  output [31:0] out_20,
  output [31:0] out_21,
  output [31:0] out_22,
  output [31:0] out_23,
  output [31:0] out_24,
  output [31:0] out_25,
  output [31:0] out_26,
  output [31:0] out_27,
  output [31:0] out_28,
  output [31:0] out_29,
  output [31:0] out_30,
  output [31:0] out_31,
  output [31:0] out_32,
  output [31:0] out_33,
  output [31:0] out_34
);

  wire _1_out, _2_out, _3_out, _4_out, _5_out, _6_out, _7_out, _8_out, _9_out, _10_out, _11_out, _12_out,
       _13_out, _14_out, _15_out, _16_out, _17_out, _18_out, _19_out, _20_out, _21_out, _22_out, _23_out,
       _24_out, _25_out, _26_out, _27_out, _28_out, _29_out, _30_out, _31_out, Clock_out, decoder_1_out1,
       decoder_1_out2, decoder_1_out3, decoder_1_out4, decoder_1_out5, decoder_1_out6, decoder_1_out7,
       decoder_1_out8, decoder_1_out9, decoder_1_out10, decoder_1_out11, decoder_1_out12, decoder_1_out13,
       decoder_1_out14, decoder_1_out15, decoder_1_out16, decoder_1_out17, decoder_1_out18, decoder_1_out19,
       decoder_1_out20, decoder_1_out21, decoder_1_out22, decoder_1_out23, decoder_1_out24, decoder_1_out25,
       decoder_1_out26, decoder_1_out27, decoder_1_out28, decoder_1_out29, decoder_1_out30, decoder_1_out31;

  Clock Clock (.out(Clock_out));
  Decoder #(.select(5)) decoder_1 (
    .out1(decoder_1_out1), .out2(decoder_1_out2), .out3(decoder_1_out3), .out4(decoder_1_out4),
    .out5(decoder_1_out5), .out6(decoder_1_out6), .out7(decoder_1_out7), .out8(decoder_1_out8),
    .out9(decoder_1_out9), .out10(decoder_1_out10), .out11(decoder_1_out11), .out12(decoder_1_out12),
    .out13(decoder_1_out13), .out14(decoder_1_out14), .out15(decoder_1_out15), .out16(decoder_1_out16),
    .out17(decoder_1_out17), .out18(decoder_1_out18), .out19(decoder_1_out19), .out20(decoder_1_out20),
    .out21(decoder_1_out21), .out22(decoder_1_out22), .out23(decoder_1_out23), .out24(decoder_1_out24),
    .out25(decoder_1_out25), .out26(decoder_1_out26), .out27(decoder_1_out27), .out28(decoder_1_out28),
    .out29(decoder_1_out29), .out30(decoder_1_out30), .out31(decoder_1_out31), .sel(RW), .en(1'b1));  // open: out0
  and _25 (_25_out, decoder_1_out25, RegWrite);
  and _26 (_26_out, decoder_1_out26, RegWrite);
  and _27 (_27_out, decoder_1_out27, RegWrite);
  and _28 (_28_out, decoder_1_out28, RegWrite);
  and _29 (_29_out, decoder_1_out29, RegWrite);
  and _30 (_30_out, decoder_1_out30, RegWrite);
  and _31 (_31_out, decoder_1_out31, RegWrite);
  Register #(.width(32)) R25 (.D(BusW), .en(_25_out), .Q(out_22), .clk(Clock_out));  // open: clr
  Register #(.width(32)) R26 (.D(BusW), .en(_26_out), .Q(out_24), .clk(Clock_out));  // open: clr
  Register #(.width(32)) R27 (.D(BusW), .en(_27_out), .Q(out_26), .clk(Clock_out));  // open: clr
  Register #(.width(32)) R28 (.D(BusW), .en(_28_out), .Q(out_28), .clk(Clock_out));  // open: clr
  Register #(.width(32)) R29 (.D(BusW), .en(_29_out), .Q(out_30), .clk(Clock_out));  // open: clr
  Register #(.width(32)) R30 (.D(BusW), .en(_30_out), .Q(out_32), .clk(Clock_out));  // open: clr
  Register #(.width(32)) R31 (.D(BusW), .en(_31_out), .Q(out_34), .clk(Clock_out));  // open: clr
  and _17 (_17_out, decoder_1_out17, RegWrite);
  and _18 (_18_out, decoder_1_out18, RegWrite);
  and _19 (_19_out, decoder_1_out19, RegWrite);
  and _20 (_20_out, decoder_1_out20, RegWrite);
  and _21 (_21_out, decoder_1_out21, RegWrite);
  and _22 (_22_out, decoder_1_out22, RegWrite);
  and _23 (_23_out, decoder_1_out23, RegWrite);
  and _24 (_24_out, decoder_1_out24, RegWrite);
  Register #(.width(32)) R17 (.D(BusW), .en(_17_out), .Q(out_18), .clk(Clock_out));  // open: clr
  Register #(.width(32)) R18 (.D(BusW), .en(_18_out), .Q(out_20), .clk(Clock_out));  // open: clr
  Register #(.width(32)) R19 (.D(BusW), .en(_19_out), .Q(out_23), .clk(Clock_out));  // open: clr
  Register #(.width(32)) R20 (.D(BusW), .en(_20_out), .Q(out_25), .clk(Clock_out));  // open: clr
  Register #(.width(32)) R21 (.D(BusW), .en(_21_out), .Q(out_27), .clk(Clock_out));  // open: clr
  Register #(.width(32)) R22 (.D(BusW), .en(_22_out), .Q(out_29), .clk(Clock_out));  // open: clr
  Register #(.width(32)) R23 (.D(BusW), .en(_23_out), .Q(out_31), .clk(Clock_out));  // open: clr
  Register #(.width(32)) R24 (.D(BusW), .en(_24_out), .Q(out_33), .clk(Clock_out));  // open: clr
  and _9 (_9_out, decoder_1_out9, RegWrite);
  and _10 (_10_out, decoder_1_out10, RegWrite);
  and _11 (_11_out, decoder_1_out11, RegWrite);
  and _12 (_12_out, decoder_1_out12, RegWrite);
  and _13 (_13_out, decoder_1_out13, RegWrite);
  and _14 (_14_out, decoder_1_out14, RegWrite);
  and _15 (_15_out, decoder_1_out15, RegWrite);
  and _16 (_16_out, decoder_1_out16, RegWrite);
  and _1 (_1_out, decoder_1_out1, RegWrite);
  and _2 (_2_out, decoder_1_out2, RegWrite);
  and _3 (_3_out, decoder_1_out3, RegWrite);
  and _4 (_4_out, decoder_1_out4, RegWrite);
  and _5 (_5_out, decoder_1_out5, RegWrite);
  and _6 (_6_out, decoder_1_out6, RegWrite);
  and _7 (_7_out, decoder_1_out7, RegWrite);
  and _8 (_8_out, decoder_1_out8, RegWrite);
  Register #(.width(32)) R9 (.D(BusW), .en(_9_out), .Q(out_12), .clk(Clock_out));  // open: clr
  Register #(.width(32)) R10 (.D(BusW), .en(_10_out), .Q(out_13), .clk(Clock_out));  // open: clr
  Register #(.width(32)) R11 (.D(BusW), .en(_11_out), .Q(out_14), .clk(Clock_out));  // open: clr
  Register #(.width(32)) R12 (.D(BusW), .en(_12_out), .Q(out_15), .clk(Clock_out));  // open: clr
  Register #(.width(32)) R13 (.D(BusW), .en(_13_out), .Q(out_16), .clk(Clock_out));  // open: clr
  Register #(.width(32)) R14 (.D(BusW), .en(_14_out), .Q(out_17), .clk(Clock_out));  // open: clr
  Register #(.width(32)) R15 (.D(BusW), .en(_15_out), .Q(out_19), .clk(Clock_out));  // open: clr
  Register #(.width(32)) R16 (.D(BusW), .en(_16_out), .Q(out_21), .clk(Clock_out));  // open: clr
  Register #(.width(32)) R1 (.D(BusW), .en(_1_out), .Q(out_4), .clk(Clock_out));  // open: clr
  Register #(.width(32)) R2 (.D(BusW), .en(_2_out), .Q(out_5), .clk(Clock_out));  // open: clr
  Register #(.width(32)) R3 (.D(BusW), .en(_3_out), .Q(out_6), .clk(Clock_out));  // open: clr
  Register #(.width(32)) R4 (.D(BusW), .en(_4_out), .Q(out_7), .clk(Clock_out));  // open: clr
  Register #(.width(32)) R5 (.D(BusW), .en(_5_out), .Q(out_8), .clk(Clock_out));  // open: clr
  Register #(.width(32)) R6 (.D(BusW), .en(_6_out), .Q(out_9), .clk(Clock_out));  // open: clr
  Register #(.width(32)) R7 (.D(BusW), .en(_7_out), .Q(out_10), .clk(Clock_out));  // open: clr
  Register #(.width(32)) R8 (.D(BusW), .en(_8_out), .Q(out_11), .clk(Clock_out));  // open: clr
endmodule

module Stage2 (
);

  main main_1 ();  // open: BusW, RegWrite, RW, out_4, out_5, out_6, out_7, out_8, out_9, out_10, out_11, out_12, out_13, out_14, out_15, out_16, out_17, out_18, out_19, out_20, out_21, out_22, out_23, out_24, out_25, out_26, out_27, out_28, out_29, out_30, out_31, out_32, out_33, out_34
endmodule
